// Logisim project 8BitComputer.circ as structural Verilog: 36 circuits, main circuit CPU
module BasicMemory (
  input  in_1,
  input  in_2,
  output out_3
);

  wire nand_1_out, nand_2_out, nand_4_out;

  nand nand_1 (nand_1_out, in_1, in_2);
  nand nand_2 (nand_2_out, nand_1_out, in_2);
  nand nand_3 (out_3, nand_1_out, nand_4_out);
  nand nand_4 (nand_4_out, out_3, nand_2_out);

  // Notes on the sheet:
  //   in_2: pull=down
  //   in_1: pull=down
endmodule

module Memory8 (
  input  [7:0] in_1,
  input  s,
  output [7:0] out_3
);

  BasicMemory basicmemory_1 (.in_1(in_1[0]), .in_2(s), .out_3(out_3[0]));
  BasicMemory basicmemory_2 (.in_1(in_1[1]), .in_2(s), .out_3(out_3[1]));
  BasicMemory basicmemory_3 (.in_1(in_1[2]), .in_2(s), .out_3(out_3[2]));
  BasicMemory basicmemory_4 (.in_1(in_1[3]), .in_2(s), .out_3(out_3[3]));
  BasicMemory basicmemory_5 (.in_1(in_1[4]), .in_2(s), .out_3(out_3[4]));
  BasicMemory basicmemory_6 (.in_1(in_1[5]), .in_2(s), .out_3(out_3[5]));
  BasicMemory basicmemory_7 (.in_1(in_1[6]), .in_2(s), .out_3(out_3[6]));
  BasicMemory basicmemory_8 (.in_1(in_1[7]), .in_2(s), .out_3(out_3[7]));

  // Notes on the sheet:
  //   out_3: pull=down
  //   in_1: pull=down
  //   s: pull=down
endmodule

module Register8 (
  input  [7:0] i,
  input  s,
  input  e,
  output [7:0] REG,
  output [7:0] _0
);

  wire [7:0] enabler_1_out_3;

  Memory8 memory8_1 (.s(s), .in_1(i), .out_3(REG));
  Enabler enabler_1 (.in_1(REG), .out_3(enabler_1_out_3), .in_2(e));
  assign _0 = e ? enabler_1_out_3 : 8'bz;  // Controlled_Buffer controlled_buffer_1

  // Notes on the sheet:
  //   i: pull=down
  //   s: pull=down
  //   e: pull=down
  //   _0: pull=down
endmodule

module Decoder4x16 (
  input  [3:0] in_1,
  output L,
  output out_3,
  output out_4,
  output out_5,
  output out_6,
  output out_7,
  output out_8,
  output out_9,
  output out_10,
  output out_11,
  output out_12,
  output out_13,
  output out_14,
  output out_15,
  output out_16,
  output M
);

  wire not_1_out, not_2_out, not_3_out, not_4_out;

  not not_1 (not_1_out, in_1[0]);
  not not_2 (not_2_out, in_1[1]);
  not not_3 (not_3_out, in_1[2]);
  not not_4 (not_4_out, in_1[3]);
  and and_1 (L, not_4_out, not_3_out, not_2_out, not_1_out);
  and and_2 (out_3, not_4_out, not_3_out, not_2_out, in_1[0]);
  and and_3 (out_4, not_4_out, not_3_out, in_1[1], not_1_out);
  and and_4 (out_5, not_4_out, not_3_out, in_1[1], in_1[0]);
  and and_5 (out_6, not_4_out, in_1[2], not_2_out, not_1_out);
  and and_6 (out_7, not_4_out, in_1[2], not_2_out, in_1[0]);
  and and_7 (out_8, not_4_out, in_1[2], in_1[1], not_1_out);
  and and_8 (out_9, not_4_out, in_1[2], in_1[1], in_1[0]);
  and and_9 (out_10, in_1[3], not_3_out, not_2_out, not_1_out);
  and and_10 (out_11, in_1[3], not_3_out, not_2_out, in_1[0]);
  and and_11 (out_12, in_1[3], not_3_out, in_1[1], not_1_out);
  and and_12 (out_13, in_1[3], not_3_out, in_1[1], in_1[0]);
  and and_13 (out_14, in_1[3], in_1[2], not_2_out, not_1_out);
  and and_14 (out_15, in_1[3], in_1[2], not_2_out, in_1[0]);
  and and_15 (out_16, in_1[3], in_1[2], in_1[1], not_1_out);
  and and_16 (M, in_1[3], in_1[2], in_1[1], in_1[0]);

  // Notes on the sheet:
  //   out_4: pull=down
  //   out_8: pull=down
  //   out_11: pull=down
  //   out_9: pull=down
  //   out_3: pull=down
  //   out_16: pull=down
  //   out_5: pull=down
  //   out_6: pull=down
  //   out_13: pull=down
  //   out_10: pull=down
  //   out_15: pull=down
  //   L: pull=down
  //   out_14: pull=down
  //   out_7: pull=down
  //   out_12: pull=down
  //   in_1: pull=down
  //   M: pull=down
endmodule

module RegisterByte (
  input  [7:0] i,
  input  RESET,
  input  h,
  input  v,
  input  s,
  input  e,
  output [7:0] o,
  output [7:0] op
);

  wire and_1_out, and_2_out, and_3_out, or_1_out;
  wire [7:0] register8_1__0;

  and and_1 (and_1_out, h, v);
  and and_2 (and_2_out, and_1_out, s);
  and and_3 (and_3_out, and_1_out, e);
  or or_1 (or_1_out, RESET, and_2_out);
  Register8 register8_1 (.i(i), .s(or_1_out), .e(and_3_out), ._0(register8_1__0), .REG(op));
  assign o = and_3_out ? register8_1__0 : 8'bz;  // Controlled_Buffer controlled_buffer_1

  // Notes on the sheet:
  //   h: pull=down
  //   v: pull=down
  //   o: pull=down
  //   i: pull=down
  //   e: pull=down
  //   s: pull=down
  //   RESET: pull=down
  //   op: pull=down
endmodule

module Ram (
  input  reset,
  input  [7:0] i,
  input  sa,
  input  [7:0] address,
  input  s,
  input  e,
  output [7:0] o,
  output [7:0] _15,
  output [7:0] _14,
  output [7:0] _13,
  output [7:0] _12,
  output [7:0] _11,
  output [7:0] _10,
  output [7:0] _9,
  output [7:0] _8,
  output [7:0] _7,
  output [7:0] _6,
  output [7:0] _5,
  output [7:0] _4,
  output [7:0] _21,
  output [7:0] _2,
  output [7:0] _1,
  output [7:0] _0,
  output [7:0] _31,
  output [7:0] _30,
  output [7:0] _29,
  output [7:0] _28,
  output [7:0] _27,
  output [7:0] _26,
  output [7:0] _25,
  output [7:0] _24,
  output [7:0] _23,
  output [7:0] _22,
  output [7:0] _21_2,
  output [7:0] _20,
  output [7:0] _19,
  output [7:0] _18,
  output [7:0] _17,
  output [7:0] _16,
  output [7:0] _47,
  output [7:0] _46,
  output [7:0] _45,
  output [7:0] _44,
  output [7:0] _43,
  output [7:0] _42,
  output [7:0] _41,
  output [7:0] _40,
  output [7:0] _39,
  output [7:0] _38,
  output [7:0] _37,
  output [7:0] _36,
  output [7:0] _35,
  output [7:0] _34,
  output [7:0] _33,
  output [7:0] _32,
  output [7:0] _63,
  output [7:0] _62,
  output [7:0] _61,
  output [7:0] _60,
  output [7:0] _59,
  output [7:0] _58,
  output [7:0] _57,
  output [7:0] _56,
  output [7:0] _55,
  output [7:0] _54,
  output [7:0] _53,
  output [7:0] _52,
  output [7:0] _51,
  output [7:0] _50,
  output [7:0] _49,
  output [7:0] _48,
  output [7:0] _79,
  output [7:0] _78,
  output [7:0] _77,
  output [7:0] _76,
  output [7:0] _75,
  output [7:0] _74,
  output [7:0] _73,
  output [7:0] _72,
  output [7:0] _71,
  output [7:0] _70,
  output [7:0] _69,
  output [7:0] _68,
  output [7:0] _67,
  output [7:0] _66,
  output [7:0] _65,
  output [7:0] _64,
  output [7:0] _95,
  output [7:0] _94,
  output [7:0] _93,
  output [7:0] _92,
  output [7:0] _91,
  output [7:0] _90,
  output [7:0] _89,
  output [7:0] _88,
  output [7:0] _87,
  output [7:0] _86,
  output [7:0] _85,
  output [7:0] _84,
  output [7:0] _83,
  output [7:0] _82,
  output [7:0] _81,
  output [7:0] _80,
  output [7:0] _111,
  output [7:0] _110,
  output [7:0] _109,
  output [7:0] _108,
  output [7:0] _107,
  output [7:0] _106,
  output [7:0] _105,
  output [7:0] _104,
  output [7:0] _103,
  output [7:0] _102,
  output [7:0] _101,
  output [7:0] _100,
  output [7:0] _99,
  output [7:0] _98,
  output [7:0] _97,
  output [7:0] _96,
  output [7:0] _127,
  output [7:0] _126,
  output [7:0] _125,
  output [7:0] _124,
  output [7:0] _123,
  output [7:0] _122,
  output [7:0] _121,
  output [7:0] _120,
  output [7:0] _119,
  output [7:0] _118,
  output [7:0] _117,
  output [7:0] _116,
  output [7:0] _115,
  output [7:0] _114,
  output [7:0] _113,
  output [7:0] _112,
  output [7:0] _143,
  output [7:0] _142,
  output [7:0] _141,
  output [7:0] _140,
  output [7:0] _139,
  output [7:0] _138,
  output [7:0] _137,
  output [7:0] _136,
  output [7:0] _135,
  output [7:0] _134,
  output [7:0] _133,
  output [7:0] _132,
  output [7:0] _131,
  output [7:0] _130,
  output [7:0] _129,
  output [7:0] _128,
  output [7:0] _159,
  output [7:0] _158,
  output [7:0] _157,
  output [7:0] _156,
  output [7:0] _155,
  output [7:0] _154,
  output [7:0] _153,
  output [7:0] _152,
  output [7:0] _151,
  output [7:0] _150,
  output [7:0] _149,
  output [7:0] _148,
  output [7:0] _147,
  output [7:0] _146,
  output [7:0] _145,
  output [7:0] _144,
  output [7:0] _175,
  output [7:0] _174,
  output [7:0] _173,
  output [7:0] _172,
  output [7:0] _171,
  output [7:0] _170,
  output [7:0] _169,
  output [7:0] _168,
  output [7:0] _167,
  output [7:0] _166,
  output [7:0] _165,
  output [7:0] _164,
  output [7:0] _163,
  output [7:0] _162,
  output [7:0] _161,
  output [7:0] _160,
  output [7:0] _191,
  output [7:0] _190,
  output [7:0] _189,
  output [7:0] _188,
  output [7:0] _187,
  output [7:0] _186,
  output [7:0] _185,
  output [7:0] _184,
  output [7:0] _183,
  output [7:0] _182,
  output [7:0] _181,
  output [7:0] _180,
  output [7:0] _179,
  output [7:0] _178,
  output [7:0] _177,
  output [7:0] _176,
  output [7:0] _207,
  output [7:0] _206,
  output [7:0] _205,
  output [7:0] _204,
  output [7:0] _203,
  output [7:0] _202,
  output [7:0] _201,
  output [7:0] _200,
  output [7:0] _199,
  output [7:0] _198,
  output [7:0] _197,
  output [7:0] _196,
  output [7:0] _195,
  output [7:0] _194,
  output [7:0] _193,
  output [7:0] _192,
  output [7:0] _223,
  output [7:0] _222,
  output [7:0] _221,
  output [7:0] _220,
  output [7:0] _219,
  output [7:0] _218,
  output [7:0] _217,
  output [7:0] _216,
  output [7:0] _215,
  output [7:0] _214,
  output [7:0] _213,
  output [7:0] _212,
  output [7:0] _211,
  output [7:0] _210,
  output [7:0] _209,
  output [7:0] _208,
  output [7:0] _239,
  output [7:0] _238,
  output [7:0] _237,
  output [7:0] _236,
  output [7:0] _235,
  output [7:0] _234,
  output [7:0] _233,
  output [7:0] _232,
  output [7:0] _231,
  output [7:0] _230,
  output [7:0] _229,
  output [7:0] _228,
  output [7:0] _227,
  output [7:0] _226,
  output [7:0] _225,
  output [7:0] _224,
  output [7:0] _255,
  output [7:0] _254,
  output [7:0] _253,
  output [7:0] _252,
  output [7:0] _251,
  output [7:0] _250,
  output [7:0] _249,
  output [7:0] _248,
  output [7:0] _247,
  output [7:0] _246,
  output [7:0] _245,
  output [7:0] _244,
  output [7:0] _243,
  output [7:0] _242,
  output [7:0] _241,
  output [7:0] _240
);

  wire decoder4x16_1_l, decoder4x16_1_m, decoder4x16_1_out_3, decoder4x16_1_out_4, decoder4x16_1_out_5,
       decoder4x16_1_out_6, decoder4x16_1_out_7, decoder4x16_1_out_8, decoder4x16_1_out_9,
       decoder4x16_1_out_10, decoder4x16_1_out_11, decoder4x16_1_out_12, decoder4x16_1_out_13,
       decoder4x16_1_out_14, decoder4x16_1_out_15, decoder4x16_1_out_16, decoder4x16_2_l, decoder4x16_2_m,
       decoder4x16_2_out_3, decoder4x16_2_out_4, decoder4x16_2_out_5, decoder4x16_2_out_6,
       decoder4x16_2_out_7, decoder4x16_2_out_8, decoder4x16_2_out_9, decoder4x16_2_out_10,
       decoder4x16_2_out_11, decoder4x16_2_out_12, decoder4x16_2_out_13, decoder4x16_2_out_14,
       decoder4x16_2_out_15, decoder4x16_2_out_16;
  wire [7:0] memory8_1_out_3, registerbyte_1_o;

  Memory8 memory8_1 (.s(sa), .in_1(address), .out_3(memory8_1_out_3));
  Decoder4x16 decoder4x16_1 (
    .in_1(memory8_1_out_3[7:4]), .L(decoder4x16_1_l), .out_3(decoder4x16_1_out_3),
    .out_4(decoder4x16_1_out_4), .out_5(decoder4x16_1_out_5), .out_6(decoder4x16_1_out_6),
    .out_7(decoder4x16_1_out_7), .out_8(decoder4x16_1_out_8), .out_9(decoder4x16_1_out_9),
    .out_10(decoder4x16_1_out_10), .out_11(decoder4x16_1_out_11), .out_12(decoder4x16_1_out_12),
    .out_13(decoder4x16_1_out_13), .out_14(decoder4x16_1_out_14), .out_15(decoder4x16_1_out_15),
    .out_16(decoder4x16_1_out_16), .M(decoder4x16_1_m));
  assign o = e ? registerbyte_1_o : 8'bz;  // Controlled_Buffer controlled_buffer_1
  RegisterByte registerbyte_1 (
    .h(decoder4x16_1_l), .v(decoder4x16_2_m), .i(i), .o(registerbyte_1_o), .s(s), .e(e), .RESET(reset),
    .op(_15));
  RegisterByte registerbyte_2 (
    .h(decoder4x16_1_out_3), .v(decoder4x16_2_m), .i(i), .o(registerbyte_1_o), .s(s), .e(e), .RESET(reset),
    .op(_31));
  RegisterByte registerbyte_3 (
    .h(decoder4x16_1_l), .v(decoder4x16_2_out_16), .i(i), .o(registerbyte_1_o), .s(s), .e(e), .RESET(reset),
    .op(_14));
  RegisterByte registerbyte_4 (
    .h(decoder4x16_1_out_3), .v(decoder4x16_2_out_16), .i(i), .o(registerbyte_1_o), .s(s), .e(e),
    .RESET(reset), .op(_30));
  RegisterByte registerbyte_5 (
    .h(decoder4x16_1_l), .v(decoder4x16_2_out_15), .i(i), .o(registerbyte_1_o), .s(s), .e(e), .RESET(reset),
    .op(_13));
  RegisterByte registerbyte_6 (
    .h(decoder4x16_1_out_3), .v(decoder4x16_2_out_15), .i(i), .o(registerbyte_1_o), .s(s), .e(e),
    .RESET(reset), .op(_29));
  RegisterByte registerbyte_7 (
    .h(decoder4x16_1_l), .v(decoder4x16_2_out_14), .i(i), .o(registerbyte_1_o), .s(s), .e(e), .RESET(reset),
    .op(_12));
  RegisterByte registerbyte_8 (
    .h(decoder4x16_1_out_3), .v(decoder4x16_2_out_14), .i(i), .o(registerbyte_1_o), .s(s), .e(e),
    .RESET(reset), .op(_28));
  RegisterByte registerbyte_9 (
    .h(decoder4x16_1_l), .v(decoder4x16_2_out_13), .i(i), .o(registerbyte_1_o), .s(s), .e(e), .RESET(reset),
    .op(_11));
  RegisterByte registerbyte_10 (
    .h(decoder4x16_1_out_3), .v(decoder4x16_2_out_13), .i(i), .o(registerbyte_1_o), .s(s), .e(e),
    .RESET(reset), .op(_27));
  RegisterByte registerbyte_11 (
    .h(decoder4x16_1_l), .v(decoder4x16_2_out_12), .i(i), .o(registerbyte_1_o), .s(s), .e(e), .RESET(reset),
    .op(_10));
  RegisterByte registerbyte_12 (
    .h(decoder4x16_1_out_3), .v(decoder4x16_2_out_12), .i(i), .o(registerbyte_1_o), .s(s), .e(e),
    .RESET(reset), .op(_26));
  RegisterByte registerbyte_13 (
    .h(decoder4x16_1_l), .v(decoder4x16_2_out_11), .i(i), .o(registerbyte_1_o), .s(s), .e(e), .RESET(reset),
    .op(_9));
  RegisterByte registerbyte_14 (
    .h(decoder4x16_1_out_3), .v(decoder4x16_2_out_11), .i(i), .o(registerbyte_1_o), .s(s), .e(e),
    .RESET(reset), .op(_25));
  RegisterByte registerbyte_15 (
    .h(decoder4x16_1_l), .v(decoder4x16_2_out_10), .i(i), .o(registerbyte_1_o), .s(s), .e(e), .RESET(reset),
    .op(_8));
  RegisterByte registerbyte_16 (
    .h(decoder4x16_1_out_3), .v(decoder4x16_2_out_10), .i(i), .o(registerbyte_1_o), .s(s), .e(e),
    .RESET(reset), .op(_24));
  Decoder4x16 decoder4x16_2 (
    .in_1(memory8_1_out_3[3:0]), .L(decoder4x16_2_l), .out_3(decoder4x16_2_out_3),
    .out_4(decoder4x16_2_out_4), .out_5(decoder4x16_2_out_5), .out_6(decoder4x16_2_out_6),
    .out_7(decoder4x16_2_out_7), .out_8(decoder4x16_2_out_8), .out_9(decoder4x16_2_out_9),
    .out_10(decoder4x16_2_out_10), .out_11(decoder4x16_2_out_11), .out_12(decoder4x16_2_out_12),
    .out_13(decoder4x16_2_out_13), .out_14(decoder4x16_2_out_14), .out_15(decoder4x16_2_out_15),
    .out_16(decoder4x16_2_out_16), .M(decoder4x16_2_m));
  RegisterByte registerbyte_17 (
    .h(decoder4x16_1_l), .v(decoder4x16_2_out_9), .i(i), .o(registerbyte_1_o), .s(s), .e(e), .RESET(reset),
    .op(_7));
  RegisterByte registerbyte_18 (
    .h(decoder4x16_1_out_3), .v(decoder4x16_2_out_9), .i(i), .o(registerbyte_1_o), .s(s), .e(e),
    .RESET(reset), .op(_23));
  RegisterByte registerbyte_19 (
    .h(decoder4x16_1_l), .v(decoder4x16_2_out_8), .i(i), .o(registerbyte_1_o), .s(s), .e(e), .RESET(reset),
    .op(_6));
  RegisterByte registerbyte_20 (
    .h(decoder4x16_1_out_3), .v(decoder4x16_2_out_8), .i(i), .o(registerbyte_1_o), .s(s), .e(e),
    .RESET(reset), .op(_22));
  RegisterByte registerbyte_21 (
    .h(decoder4x16_1_l), .v(decoder4x16_2_out_7), .i(i), .o(registerbyte_1_o), .s(s), .e(e), .RESET(reset),
    .op(_5));
  RegisterByte registerbyte_22 (
    .h(decoder4x16_1_out_3), .v(decoder4x16_2_out_7), .i(i), .o(registerbyte_1_o), .s(s), .e(e),
    .RESET(reset), .op(_21_2));
  RegisterByte registerbyte_23 (
    .h(decoder4x16_1_l), .v(decoder4x16_2_out_6), .i(i), .o(registerbyte_1_o), .s(s), .e(e), .RESET(reset),
    .op(_4));
  RegisterByte registerbyte_24 (
    .h(decoder4x16_1_out_3), .v(decoder4x16_2_out_6), .i(i), .o(registerbyte_1_o), .s(s), .e(e),
    .RESET(reset), .op(_20));
  RegisterByte registerbyte_25 (
    .h(decoder4x16_1_l), .v(decoder4x16_2_out_5), .i(i), .o(registerbyte_1_o), .s(s), .e(e), .RESET(reset),
    .op(_21));
  RegisterByte registerbyte_26 (
    .h(decoder4x16_1_out_3), .v(decoder4x16_2_out_5), .i(i), .o(registerbyte_1_o), .s(s), .e(e),
    .RESET(reset), .op(_19));
  RegisterByte registerbyte_27 (
    .h(decoder4x16_1_l), .v(decoder4x16_2_out_4), .i(i), .o(registerbyte_1_o), .s(s), .e(e), .RESET(reset),
    .op(_2));
  RegisterByte registerbyte_28 (
    .h(decoder4x16_1_out_3), .v(decoder4x16_2_out_4), .i(i), .o(registerbyte_1_o), .s(s), .e(e),
    .RESET(reset), .op(_18));
  RegisterByte registerbyte_29 (
    .h(decoder4x16_1_l), .v(decoder4x16_2_out_3), .i(i), .o(registerbyte_1_o), .s(s), .e(e), .RESET(reset),
    .op(_1));
  RegisterByte registerbyte_30 (
    .h(decoder4x16_1_out_3), .v(decoder4x16_2_out_3), .i(i), .o(registerbyte_1_o), .s(s), .e(e),
    .RESET(reset), .op(_17));
  RegisterByte registerbyte_31 (
    .h(decoder4x16_1_l), .v(decoder4x16_2_l), .i(i), .o(registerbyte_1_o), .s(s), .e(e), .RESET(reset),
    .op(_0));
  RegisterByte registerbyte_32 (
    .h(decoder4x16_1_out_3), .v(decoder4x16_2_l), .i(i), .o(registerbyte_1_o), .s(s), .e(e), .RESET(reset),
    .op(_16));

  // Notes on the sheet:
  //   o: pull=down
  //   _0: pull=down
  //   _2: pull=up
  //   _4: pull=up
  //   sa: pull=down
  //   _7: pull=up
  //   _6: pull=up
  //   reset: pull=down
  //   address: pull=down
  //   i: pull=down
endmodule

module ALU_Not (
  input  [7:0] i,
  output [7:0] out_2
);

  not not_1 (out_2[0], i[0]);
  not not_2 (out_2[1], i[1]);
  not not_3 (out_2[2], i[2]);
  not not_4 (out_2[3], i[3]);
  not not_5 (out_2[4], i[4]);
  not not_6 (out_2[5], i[5]);
  not not_7 (out_2[6], i[6]);
  not not_8 (out_2[7], i[7]);
endmodule

module ALU_And (
  input  [7:0] a,
  input  [7:0] b,
  output [7:0] o
);

  and and_1 (o[0], a[0], b[0]);
  and and_2 (o[1], a[1], b[1]);
  and and_3 (o[2], a[2], b[2]);
  and and_4 (o[3], a[3], b[3]);
  and and_5 (o[4], a[4], b[4]);
  and and_6 (o[5], a[5], b[5]);
  and and_7 (o[6], a[6], b[6]);
  and and_8 (o[7], a[7], b[7]);
endmodule

module ALU_Or (
  input  [7:0] a,
  input  [7:0] b,
  output [7:0] _0
);

  or or_1 (_0[0], a[0], b[0]);
  or or_2 (_0[1], a[1], b[1]);
  or or_3 (_0[2], a[2], b[2]);
  or or_4 (_0[3], a[3], b[3]);
  or or_5 (_0[4], a[4], b[4]);
  or or_6 (_0[5], a[5], b[5]);
  or or_7 (_0[6], a[6], b[6]);
  or or_8 (_0[7], a[7], b[7]);
endmodule

module ALU_ShiftRight (
  input  [7:0] i,
  input  shift_in,
  output shift_out,
  output [7:0] o
);

  wire [7:1] register8_1__0;

  Register8 register8_1 (.i(i), .s(1'b1), .e(1'b1), ._0({register8_1__0, shift_out}));  // open: REG
  Register8 register8_2 (.i({shift_in, register8_1__0}), .s(1'b1), .e(1'b1), ._0(o));  // open: REG
endmodule

module ALU_ShiftLeft (
  input  shift_in,
  input  [7:0] i,
  output [7:0] o,
  output shift_out
);

  wire [6:0] register8_1__0;

  Register8 register8_1 (.i(i), .s(1'b1), .e(1'b1), ._0({shift_out, register8_1__0}));  // open: REG
  Register8 register8_2 (.i({register8_1__0, shift_in}), .s(1'b1), .e(1'b1), ._0(o));  // open: REG
endmodule

module ALU_Adder1bit (
  input  a,
  input  b,
  input  carry_in,
  output sum,
  output carry_out
);

  wire and_1_out, and_2_out, xor_1_out;

  xor xor_1 (xor_1_out, a, b);
  and and_1 (and_1_out, carry_in, xor_1_out);
  and and_2 (and_2_out, a, b);
  or or_1 (carry_out, and_1_out, and_2_out);
  xor xor_2 (sum, xor_1_out, carry_in);
endmodule

module ALU_Adder8bit (
  input  [7:0] a,
  input  [7:0] b,
  input  carry_in,
  output carry_out,
  output [7:0] out_5
);

  wire alu_adder1bit_2_carry_out, alu_adder1bit_3_carry_out, alu_adder1bit_4_carry_out,
       alu_adder1bit_5_carry_out, alu_adder1bit_6_carry_out, alu_adder1bit_7_carry_out,
       alu_adder1bit_8_carry_out;

  ALU_Adder1bit alu_adder1bit_1 (
    .a(a[7]), .b(b[7]), .carry_in(alu_adder1bit_2_carry_out), .sum(out_5[7]), .carry_out(carry_out));
  ALU_Adder1bit alu_adder1bit_2 (
    .a(a[6]), .b(b[6]), .carry_in(alu_adder1bit_3_carry_out), .sum(out_5[6]),
    .carry_out(alu_adder1bit_2_carry_out));
  ALU_Adder1bit alu_adder1bit_3 (
    .a(a[5]), .b(b[5]), .carry_in(alu_adder1bit_4_carry_out), .sum(out_5[5]),
    .carry_out(alu_adder1bit_3_carry_out));
  ALU_Adder1bit alu_adder1bit_4 (
    .a(a[4]), .b(b[4]), .carry_in(alu_adder1bit_5_carry_out), .sum(out_5[4]),
    .carry_out(alu_adder1bit_4_carry_out));
  ALU_Adder1bit alu_adder1bit_5 (
    .a(a[3]), .b(b[3]), .carry_in(alu_adder1bit_6_carry_out), .sum(out_5[3]),
    .carry_out(alu_adder1bit_5_carry_out));
  ALU_Adder1bit alu_adder1bit_6 (
    .a(a[2]), .b(b[2]), .carry_in(alu_adder1bit_7_carry_out), .sum(out_5[2]),
    .carry_out(alu_adder1bit_6_carry_out));
  ALU_Adder1bit alu_adder1bit_7 (
    .a(a[1]), .b(b[1]), .carry_in(alu_adder1bit_8_carry_out), .sum(out_5[1]),
    .carry_out(alu_adder1bit_7_carry_out));
  ALU_Adder1bit alu_adder1bit_8 (
    .a(a[0]), .b(b[0]), .carry_in(carry_in), .sum(out_5[0]), .carry_out(alu_adder1bit_8_carry_out));
endmodule

module ALU_Xor_LargerEqual (
  input  above_equal,
  input  a_larger,
  input  a,
  input  b,
  output c,
  output equal,
  output a_large
);

  wire and_2_out, not_1_out;

  xor xor_1 (c, a, b);
  not not_1 (not_1_out, c);
  and and_1 (equal, not_1_out, above_equal);
  and and_2 (and_2_out, above_equal, a, c);
  or or_1 (a_large, and_2_out, a_larger);
endmodule

module ALU_Xor8_LargerEqual (
  input  [7:0] a,
  input  [7:0] b,
  output [7:0] out_3,
  output larger,
  output equal
);

  wire alu_xor_largerequal_1_a_large, alu_xor_largerequal_1_equal, alu_xor_largerequal_2_a_large,
       alu_xor_largerequal_2_equal, alu_xor_largerequal_3_a_large, alu_xor_largerequal_3_equal,
       alu_xor_largerequal_4_a_large, alu_xor_largerequal_4_equal, alu_xor_largerequal_5_a_large,
       alu_xor_largerequal_5_equal, alu_xor_largerequal_6_a_large, alu_xor_largerequal_6_equal,
       alu_xor_largerequal_7_a_large, alu_xor_largerequal_7_equal;

  ALU_Xor_LargerEqual alu_xor_largerequal_1 (
    .a(a[7]), .b(b[7]), .a_larger(1'b0), .c(out_3[7]), .above_equal(1'b1),
    .equal(alu_xor_largerequal_1_equal), .a_large(alu_xor_largerequal_1_a_large));
  ALU_Xor_LargerEqual alu_xor_largerequal_2 (
    .a(a[6]), .b(b[6]), .a_larger(alu_xor_largerequal_1_a_large), .c(out_3[6]),
    .above_equal(alu_xor_largerequal_1_equal), .equal(alu_xor_largerequal_2_equal),
    .a_large(alu_xor_largerequal_2_a_large));
  ALU_Xor_LargerEqual alu_xor_largerequal_3 (
    .a(a[5]), .b(b[5]), .a_larger(alu_xor_largerequal_2_a_large), .c(out_3[5]),
    .above_equal(alu_xor_largerequal_2_equal), .equal(alu_xor_largerequal_3_equal),
    .a_large(alu_xor_largerequal_3_a_large));
  ALU_Xor_LargerEqual alu_xor_largerequal_4 (
    .a(a[4]), .b(b[4]), .a_larger(alu_xor_largerequal_3_a_large), .c(out_3[4]),
    .above_equal(alu_xor_largerequal_3_equal), .equal(alu_xor_largerequal_4_equal),
    .a_large(alu_xor_largerequal_4_a_large));
  ALU_Xor_LargerEqual alu_xor_largerequal_5 (
    .a(a[3]), .b(b[3]), .a_larger(alu_xor_largerequal_4_a_large), .c(out_3[3]),
    .above_equal(alu_xor_largerequal_4_equal), .equal(alu_xor_largerequal_5_equal),
    .a_large(alu_xor_largerequal_5_a_large));
  ALU_Xor_LargerEqual alu_xor_largerequal_6 (
    .a(a[2]), .b(b[2]), .a_larger(alu_xor_largerequal_5_a_large), .c(out_3[2]),
    .above_equal(alu_xor_largerequal_5_equal), .equal(alu_xor_largerequal_6_equal),
    .a_large(alu_xor_largerequal_6_a_large));
  ALU_Xor_LargerEqual alu_xor_largerequal_7 (
    .a(a[1]), .b(b[1]), .a_larger(alu_xor_largerequal_6_a_large), .c(out_3[1]),
    .above_equal(alu_xor_largerequal_6_equal), .equal(alu_xor_largerequal_7_equal),
    .a_large(alu_xor_largerequal_7_a_large));
  ALU_Xor_LargerEqual alu_xor_largerequal_8 (
    .a(a[0]), .b(b[0]), .a_larger(alu_xor_largerequal_7_a_large), .c(out_3[0]),
    .above_equal(alu_xor_largerequal_7_equal), .equal(equal), .a_large(larger));
endmodule

module Zeroer (
  input  [7:0] i,
  output o
);

  wire or_1_out;

  or or_1 (or_1_out, i[0], i[1], i[2], i[3], i[4], i[5], i[6], i[7]);
  not not_1 (o, or_1_out);
endmodule

module Decoder3x8_SingleOut (
  input  c,
  input  b,
  input  a,
  output [7:0] o
);

  wire not_1_out, not_2_out, not_3_out;

  not not_1 (not_1_out, a);
  not not_2 (not_2_out, b);
  not not_3 (not_3_out, c);
  and and_1 (o[0], not_3_out, not_2_out, not_1_out);
  and and_2 (o[1], not_3_out, not_2_out, a);
  and and_3 (o[2], not_3_out, b, not_1_out);
  and and_4 (o[3], not_3_out, b, a);
  and and_5 (o[4], c, not_2_out, not_1_out);
  and and_6 (o[5], c, not_2_out, a);
  and and_7 (o[6], c, b, not_1_out);
  and and_8 (o[7], c, b, a);

  // Notes on the sheet:
  //   o: pull=down
  //   c: pull=down
  //   b: pull=down
  //   a: pull=down
endmodule

module Enabler (
  input  [7:0] in_1,
  input  in_2,
  output [7:0] out_3
);

  wire and_1_out, and_2_out, and_3_out, and_4_out, and_5_out, and_6_out, and_7_out, and_8_out;

  assign out_3[0] = in_2 ? and_1_out : 1'bz;  // Controlled_Buffer controlled_buffer_1
  and and_1 (and_1_out, in_1[0], in_2);
  and and_2 (and_2_out, in_1[1], in_2);
  assign out_3[1] = in_2 ? and_2_out : 1'bz;  // Controlled_Buffer controlled_buffer_2
  assign out_3[2] = in_2 ? and_3_out : 1'bz;  // Controlled_Buffer controlled_buffer_3
  and and_3 (and_3_out, in_1[2], in_2);
  and and_4 (and_4_out, in_1[3], in_2);
  assign out_3[3] = in_2 ? and_4_out : 1'bz;  // Controlled_Buffer controlled_buffer_4
  and and_5 (and_5_out, in_1[4], in_2);
  assign out_3[4] = in_2 ? and_5_out : 1'bz;  // Controlled_Buffer controlled_buffer_5
  assign out_3[5] = in_2 ? and_6_out : 1'bz;  // Controlled_Buffer controlled_buffer_6
  and and_6 (and_6_out, in_1[5], in_2);
  assign out_3[6] = in_2 ? and_7_out : 1'bz;  // Controlled_Buffer controlled_buffer_7
  and and_7 (and_7_out, in_1[6], in_2);
  and and_8 (and_8_out, in_1[7], in_2);
  assign out_3[7] = in_2 ? and_8_out : 1'bz;  // Controlled_Buffer controlled_buffer_8
endmodule

module ALU (
  input  [7:0] a,
  input  [7:0] b,
  input  carry_in,
  input  a_2,
  input  b_2,
  input  c,
  output a_larger,
  output equal,
  output zero,
  output [7:0] c_2,
  output carry_out
);

  wire alu_adder8bit_1_carry_out, alu_shiftleft_1_shift_out, alu_shiftright_1_shift_out, and_1_out,
       and_2_out, and_3_out;
  wire [7:0] alu_adder8bit_1_out_5, alu_and_1_o, alu_not_1_out_2, alu_or_1__0, alu_shiftleft_1_o,
       alu_shiftright_1_o, alu_xor8_largerequal_1_out_3, decoder3x8_singleout_1_o;

  ALU_Xor8_LargerEqual alu_xor8_largerequal_1 (
    .a(a), .b(b), .out_3(alu_xor8_largerequal_1_out_3), .larger(a_larger), .equal(equal));
  ALU_And alu_and_1 (.a(a), .o(alu_and_1_o), .b(b));
  ALU_Not alu_not_1 (.i(a), .out_2(alu_not_1_out_2));
  ALU_ShiftLeft alu_shiftleft_1 (
    .shift_in(carry_in), .i(a), .o(alu_shiftleft_1_o), .shift_out(alu_shiftleft_1_shift_out));
  ALU_ShiftRight alu_shiftright_1 (
    .shift_out(alu_shiftright_1_shift_out), .i(a), .o(alu_shiftright_1_o), .shift_in(carry_in));
  ALU_Or alu_or_1 (.a(a), .b(b), ._0(alu_or_1__0));
  ALU_Adder8bit alu_adder8bit_1 (
    .a(a), .b(b), .carry_out(alu_adder8bit_1_carry_out), .out_5(alu_adder8bit_1_out_5), .carry_in(carry_in));
  Enabler enabler_1 (.in_1(alu_xor8_largerequal_1_out_3), .out_3(c_2), .in_2(decoder3x8_singleout_1_o[6]));
  Enabler enabler_2 (.in_1(alu_or_1__0), .out_3(c_2), .in_2(decoder3x8_singleout_1_o[5]));
  Enabler enabler_3 (.in_1(alu_and_1_o), .out_3(c_2), .in_2(decoder3x8_singleout_1_o[4]));
  Enabler enabler_4 (.in_1(alu_not_1_out_2), .out_3(c_2), .in_2(decoder3x8_singleout_1_o[3]));
  Enabler enabler_5 (.in_1(alu_shiftright_1_o), .out_3(c_2), .in_2(decoder3x8_singleout_1_o[1]));
  Decoder3x8_SingleOut decoder3x8_singleout_1 (.b(b_2), .o(decoder3x8_singleout_1_o), .c(c), .a(a_2));
  Enabler enabler_6 (.in_1(alu_shiftleft_1_o), .out_3(c_2), .in_2(decoder3x8_singleout_1_o[2]));
  Enabler enabler_7 (.in_1(alu_adder8bit_1_out_5), .out_3(c_2), .in_2(decoder3x8_singleout_1_o[0]));
  and and_1 (and_1_out, alu_shiftleft_1_shift_out, decoder3x8_singleout_1_o[2]);
  assign carry_out = decoder3x8_singleout_1_o[2] ? and_1_out : 1'bz;  // Controlled_Buffer controlled_buffer_1
  assign carry_out = decoder3x8_singleout_1_o[1] ? and_2_out : 1'bz;  // Controlled_Buffer controlled_buffer_2
  and and_2 (and_2_out, alu_shiftright_1_shift_out, decoder3x8_singleout_1_o[1]);
  assign carry_out = decoder3x8_singleout_1_o[0] ? and_3_out : 1'bz;  // Controlled_Buffer controlled_buffer_3
  and and_3 (and_3_out, alu_adder8bit_1_carry_out, decoder3x8_singleout_1_o[0]);
  Zeroer zeroer_1 (.i(c_2), .o(zero));

  // Notes on the sheet:
  //   a_larger: pull=down
  //   a_2: pull=down
  //   equal: pull=down
  //   carry_in: pull=down
  //   zero: pull=down
  //   c_2: pull=down
  //   b: pull=down
  //   a: pull=down
  //   carry_out: pull=down
  //   b_2: pull=down
  //   c: pull=down
endmodule

module Bus (
  input  [7:0] i,
  input  bus_1,
  output [7:0] o
);

  wire not_1_out;

  and and_1 (o[7], i[7], not_1_out);
  and and_2 (o[6], i[6], not_1_out);
  and and_3 (o[5], i[5], not_1_out);
  and and_4 (o[4], i[4], not_1_out);
  and and_5 (o[3], i[3], not_1_out);
  and and_6 (o[2], i[2], not_1_out);
  and and_7 (o[1], i[1], not_1_out);
  not not_1 (not_1_out, bus_1);
  or or_1 (o[0], i[0], bus_1);

  // Notes on the sheet:
  //   i: pull=down
  //   bus_1: pull=down
  //   o: pull=down
endmodule

module Accumulator (
  input  [7:0] i,
  input  s,
  input  e,
  output [7:0] ACC,
  output [7:0] o
);

  Register8 register8_1 (.i(i), .s(s), .e(e), ._0(o), .REG(ACC));

  // Notes on the sheet:
  //   i: pull=down
  //   e: pull=down
  //   o: pull=down
  //   s: pull=down
endmodule

module Registry_Large (
  input  [7:0] i,
  input  Store,
  input  Enable,
  output [7:0] \reg ,
  output [7:0] o
);

  Register8 register8_1 (.i(i), .s(Store), .e(Enable), ._0(o), .REG(\reg ));

  // Notes on the sheet:
  //   i: pull=down
  //   Enable: pull=down
  //   Store: pull=down
  //   o: pull=down
endmodule

module Register_Temporary (
  input  [7:0] i,
  input  s,
  output [7:0] o
);

  wire [7:0] controlled_buffer_1_out;

  assign controlled_buffer_1_out = s ? i : 8'bz;  // Controlled_Buffer controlled_buffer_1
  Memory8 memory8_1 (.s(s), .in_1(controlled_buffer_1_out), .out_3(o));

  // Notes on the sheet:
  //   i: pull=down
  //   o: pull=down
  //   s: pull=down
endmodule

module Stepper (
  input  reset,
  input  clk,
  output step_1,
  output step_2,
  output step_3,
  output step_4,
  output step_5,
  output step_6,
  output step_7
);

  wire basicmemory_1_out_3, basicmemory_2_out_3, basicmemory_3_out_3, basicmemory_4_out_3,
       basicmemory_5_out_3, basicmemory_6_out_3, basicmemory_7_out_3, basicmemory_8_out_3,
       basicmemory_9_out_3, basicmemory_10_out_3, basicmemory_11_out_3, not_1_out, not_2_out, not_3_out,
       not_4_out, not_5_out, not_6_out, not_7_out, not_8_out, or_1_out, or_2_out;

  not not_1 (not_1_out, clk);
  not not_2 (not_2_out, reset);
  or or_1 (or_1_out, reset, clk);
  or or_2 (or_2_out, reset, not_1_out);
  or or_3 (step_1, reset, not_3_out);
  BasicMemory basicmemory_1 (.in_1(not_2_out), .in_2(or_1_out), .out_3(basicmemory_1_out_3));
  not not_3 (not_3_out, basicmemory_2_out_3);
  BasicMemory basicmemory_2 (.in_1(basicmemory_1_out_3), .in_2(or_2_out), .out_3(basicmemory_2_out_3));
  and and_1 (step_2, basicmemory_2_out_3, not_4_out);
  not not_4 (not_4_out, basicmemory_4_out_3);
  BasicMemory basicmemory_3 (.in_1(basicmemory_2_out_3), .in_2(or_1_out), .out_3(basicmemory_3_out_3));
  BasicMemory basicmemory_4 (.in_1(basicmemory_3_out_3), .in_2(or_2_out), .out_3(basicmemory_4_out_3));
  and and_2 (step_3, basicmemory_4_out_3, not_5_out);
  BasicMemory basicmemory_5 (.in_1(basicmemory_4_out_3), .in_2(or_1_out), .out_3(basicmemory_5_out_3));
  not not_5 (not_5_out, basicmemory_6_out_3);
  BasicMemory basicmemory_6 (.in_1(basicmemory_5_out_3), .in_2(or_2_out), .out_3(basicmemory_6_out_3));
  and and_3 (step_4, basicmemory_6_out_3, not_6_out);
  not not_6 (not_6_out, basicmemory_8_out_3);
  BasicMemory basicmemory_7 (.in_1(basicmemory_6_out_3), .in_2(or_1_out), .out_3(basicmemory_7_out_3));
  and and_4 (step_5, basicmemory_8_out_3, not_7_out);
  BasicMemory basicmemory_8 (.in_1(basicmemory_7_out_3), .in_2(or_2_out), .out_3(basicmemory_8_out_3));
  BasicMemory basicmemory_9 (.in_1(basicmemory_8_out_3), .in_2(or_1_out), .out_3(basicmemory_9_out_3));
  not not_7 (not_7_out, basicmemory_10_out_3);
  BasicMemory basicmemory_10 (.in_1(basicmemory_9_out_3), .in_2(or_2_out), .out_3(basicmemory_10_out_3));
  and and_5 (step_6, basicmemory_10_out_3, not_8_out);
  BasicMemory basicmemory_11 (.in_1(basicmemory_10_out_3), .in_2(or_1_out), .out_3(basicmemory_11_out_3));
  not not_8 (not_8_out, step_7);
  BasicMemory basicmemory_12 (.in_1(basicmemory_11_out_3), .in_2(or_2_out), .out_3(step_7));

  // Notes on the sheet:
  //   reset: pull=down
endmodule

module CPU (
  input  clock,
  input  Load,
  input  MARS,
  input  Reset,
  input  [7:0] Ram_In,
  output clkl,
  output clke,
  output clks,
  output End,
  output S,
  output E,
  output IO,
  output DA,
  output [7:0] Bus_Out
);

  wire alu_1_a_larger, alu_1_carry_out, alu_1_equal, alu_1_zero, and_1_out, and_2_out, and_3_out, C,
       carrytemp_1_o, controller_1_acc_e, controller_1_acc_s, controller_1_alu_0, controller_1_alu_1,
       controller_1_alu_2, controller_1_bus, controller_1_flags_s, controller_1_iar_e, controller_1_iar_s,
       controller_1_ir_s, controller_1_mar_s, controller_1_r0_s, controller_1_r1_s, controller_1_r2_s,
       controller_1_r3_s, controller_1_ram_e, controller_1_ram_s, controller_1_register_3,
       controller_1_registry_0, controller_1_registry_1, controller_1_registry_2, flags_1_a_2, flags_1_c_2,
       flags_1_e_2, flags_1_z_2, not_1_out, S_t;
  wire [7:0] alu_1_c_2, bus_1_o, multiplexer_1_out, n256_count_loader_1_count, ram_1__56,
       register_temporary_1_o, registry_information_1_o;

  Accumulator accumulator_1 (.i(alu_1_c_2), .o(Bus_Out), .s(controller_1_acc_s), .e(controller_1_acc_e));  // open: ACC
  Register_Temporary register_temporary_1 (.i(Bus_Out), .o(register_temporary_1_o), .s(S_t));
  Bus bus_1 (.i(register_temporary_1_o), .bus_1(controller_1_bus), .o(bus_1_o));
  and and_1 (and_1_out, carrytemp_1_o, C);
  ALU alu_1 (
    .a(Bus_Out), .b(bus_1_o), .carry_in(and_1_out), .a_2(controller_1_alu_0), .b_2(controller_1_alu_1),
    .c(controller_1_alu_2), .zero(alu_1_zero), .c_2(alu_1_c_2), .carry_out(alu_1_carry_out),
    .a_larger(alu_1_a_larger), .equal(alu_1_equal));
  and and_2 (and_2_out, clock, not_1_out);
  CarryTemp carrytemp_1 (.c(flags_1_c_2), .o(carrytemp_1_o), .s(S_t));
  Flags flags_1 (
    .C(alu_1_carry_out), .A(alu_1_a_larger), .E(alu_1_equal), .Z(alu_1_zero), .C_2(flags_1_c_2),
    .A_2(flags_1_a_2), .E_2(flags_1_e_2), .Z_2(flags_1_z_2), .s(controller_1_flags_s));
  not not_1 (not_1_out, End);
  Clock clock_1 (.clkin(and_2_out), .clks(clks), .clke(clke), .clk(clkl));
  and and_3 (and_3_out, Load, clkl);
  Controller controller_1 (
    .clks(clks), .clke(clke), .clk(clkl), .MAR_S(controller_1_mar_s), .ACC_S(controller_1_acc_s),
    .TMP_S(S_t), .FLAGS_S(controller_1_flags_s), .RAM_S(controller_1_ram_s), .IO_CLKS_S(S),
    .IAR_E(controller_1_iar_e), .RAM_E(controller_1_ram_e), .IO_CLK_E(E), .Bus(controller_1_bus),
    .ACC_E(controller_1_acc_e), .IR_S(controller_1_ir_s), .IAR_S(controller_1_iar_s),
    .R0_S(controller_1_r0_s), .R1_S(controller_1_r1_s), .R2_S(controller_1_r2_s), .R3_S(controller_1_r3_s),
    .Registry_0(controller_1_registry_0), .Registry_1(controller_1_registry_1),
    .Registry_2(controller_1_registry_2), .Register_3(controller_1_register_3),
    .IR_IN(registry_information_1_o), .ALU_0(controller_1_alu_0), .ALU_1(controller_1_alu_1),
    .ALU_2(controller_1_alu_2), .C(flags_1_c_2), .A(flags_1_a_2), .E(flags_1_e_2), .Z(flags_1_z_2), .IO(IO),
    .DA(DA), .RESET(Reset), .C_2(C), .LOAD(Load), .END(End), .MARS(MARS));
  _256_count_loader u_256_count_loader_1 (.count(n256_count_loader_1_count), .clk(and_3_out));  // open: carry
  assign Bus_Out = Load ? n256_count_loader_1_count : 8'bz;  // Controlled_Buffer controlled_buffer_1
  Registry_Large registry_large_1 (
    .i(Bus_Out), .o(Bus_Out), .Store(controller_1_r0_s), .Enable(controller_1_registry_0));  // open: reg
  Registry_Address registry_address_1 (
    .i(Bus_Out), .o(Bus_Out), .s(controller_1_iar_s), .e(controller_1_iar_e));  // open: IAR
  Registry_Large registry_large_2 (
    .i(Bus_Out), .o(Bus_Out), .Store(controller_1_r1_s), .Enable(controller_1_registry_1));  // open: reg
  Registry_Large registry_large_3 (
    .i(Bus_Out), .o(Bus_Out), .Store(controller_1_r2_s), .Enable(controller_1_registry_2));  // open: reg
  Registry_Information registry_information_1 (.i(Bus_Out), .o(registry_information_1_o), .s(controller_1_ir_s));
  Registry_Large registry_large_4 (
    .i(Bus_Out), .o(Bus_Out), .Store(controller_1_r3_s), .Enable(controller_1_register_3));  // open: reg
  Multiplexer #(.width(8)) multiplexer_1 (.in0(Bus_Out), .in1(Ram_In), .out(multiplexer_1_out), .sel(Load), .en(Load));
  Ram ram_1 (
    .o(Bus_Out), .sa(controller_1_mar_s), .address(Bus_Out), .s(controller_1_ram_s), .e(controller_1_ram_e),
    .i(multiplexer_1_out), .reset(Reset), ._56(ram_1__56), ._55(ram_1__56));  // open: _0, _2, _4, _6, _7, _8, _9, _10, _11, _12, _13, _14, _15, _31, _30, _29, _28, _27, _26, _25, _24, _23, _22, _21_2, _20, _19, _18, _17, _16, _46, _47, _45, _44, _43, _42, _41, _40, _39, _38, _37, _36, _35, _34, _32, _63, _62, _61, _60, _59, _58, _57, _54, _53, _52, _51, _50, _49, _48, _5, _1, _79, _78, _74, _77, _76, _75, _73, _72, _71, _70, _69, _68, _67, _66, _65, _64, _109, _108, _107, _106, _105, _111, _110, _104, _103, _102, _101, _100, _99, _98, _97, _96, _95, _94, _93, _92, _91, _90, _89, _88, _87, _86, _84, _83, _82, _81, _80, _85, _143, _142, _141, _140, _139, _138, _137, _136, _135, _134, _133, _132, _131, _130, _129, _128, _127, _126, _125, _124, _123, _122, _121, _120, _119, _118, _117, _116, _115, _114, _113, _112, _159, _158, _157, _156, _155, _154, _153, _152, _151, _150, _149, _148, _147, _146, _145, _144, _33, _191, _190, _189, _188, _187, _186, _185, _184, _183, _182, _181, _180, _179, _178, _177, _176, _175, _174, _173, _172, _171, _170, _169, _168, _167, _166, _165, _164, _163, _162, _161, _160, _239, _238, _237, _236, _235, _234, _233, _232, _231, _230, _229, _228, _227, _226, _225, _224, _255, _254, _253, _252, _251, _250, _249, _248, _247, _246, _245, _244, _243, _242, _241, _240, _223, _222, _221, _220, _219, _218, _217, _216, _215, _214, _213, _212, _211, _210, _209, _208, _207, _206, _205, _204, _203, _202, _201, _200, _198, _197, _196, _195, _194, _193, _192, _199, _21

  // Notes on the sheet:
  //   Bus_Out: pull=down
endmodule

module Registry_Address (
  input  [7:0] i,
  input  s,
  input  e,
  output [7:0] IAR,
  output [7:0] o
);

  Register8 register8_1 (.i(i), .s(s), .e(e), ._0(o), .REG(IAR));

  // Notes on the sheet:
  //   e: pull=down
  //   i: pull=down
  //   o: pull=down
  //   s: pull=down
endmodule

module Registry_Information (
  input  [7:0] i,
  input  s,
  output [7:0] o
);

  Memory8 memory8_1 (.s(s), .in_1(i), .out_3(o));

  // Notes on the sheet:
  //   s: pull=down
  //   i: pull=down
  //   o: pull=down
endmodule

module Flags (
  input  C,
  input  A,
  input  E,
  input  Z,
  input  s,
  output C_2,
  output A_2,
  output E_2,
  output Z_2
);

  BasicMemory basicmemory_1 (.in_1(C), .in_2(s), .out_3(C_2));
  BasicMemory basicmemory_2 (.in_1(A), .in_2(s), .out_3(A_2));
  BasicMemory basicmemory_3 (.in_1(E), .in_2(s), .out_3(E_2));
  BasicMemory basicmemory_4 (.in_1(Z), .in_2(s), .out_3(Z_2));

  // Notes on the sheet:
  //   Z_2: pull=down
  //   E_2: pull=down
  //   E: pull=down
  //   Z: pull=down
  //   C_2: pull=down
  //   A: pull=down
  //   A_2: pull=down
  //   C: pull=down
endmodule

module Controller (
  input  clks,
  input  clk,
  input  clke,
  input  LOAD,
  input  MARS,
  input  RESET,
  input  C,
  input  A,
  input  E,
  input  Z,
  input  [7:0] IR_IN,
  output Bus,
  output IR_S,
  output MAR_S,
  output IAR_E,
  output IAR_S,
  output RAM_E,
  output ACC_S,
  output ACC_E,
  output RAM_S,
  output C_2,
  output TMP_S,
  output IO_CLK_E,
  output FLAGS_S,
  output IO_CLKS_S,
  output R0_S,
  output Registry_0,
  output R1_S,
  output Registry_1,
  output Registry_2,
  output R2_S,
  output Register_3,
  output R3_S,
  output END,
  output IO,
  output DA,
  output ALU_0,
  output ALU_1,
  output ALU_2
);

  wire and_5_out, and_6_out, and_7_out, and_8_out, and_9_out, and_10_out, and_11_out, and_12_out, and_16_out,
       and_17_out, and_18_out, and_19_out, and_20_out, and_21_out, and_22_out, and_23_out, and_24_out,
       and_25_out, and_26_out, and_27_out, and_28_out, and_29_out, and_30_out, and_31_out, and_32_out,
       and_33_out, and_34_out, and_35_out, and_36_out, and_37_out, and_38_out, and_39_out, and_42_out,
       and_43_out, and_44_out, and_45_out, and_46_out, and_47_out, and_48_out, and_49_out, and_50_out,
       and_51_out, and_52_out, and_53_out, and_54_out, and_55_out, and_56_out, and_57_out, and_58_out,
       and_60_out, and_61_out, and_62_out, and_63_out, decoder2x4_1__0, decoder2x4_1__1, decoder2x4_1__2,
       decoder2x4_1__3, decoder2x4_flipped_1__0, decoder2x4_flipped_1__1, decoder2x4_flipped_1__2,
       decoder2x4_flipped_1__3, decoder2x4_flipped_2__0, decoder2x4_flipped_2__1, decoder2x4_flipped_2__2,
       decoder2x4_flipped_2__3, decoder3x8_1__0, decoder3x8_1__1, decoder3x8_1__2, decoder3x8_1__3,
       decoder3x8_1__4, decoder3x8_1__5, decoder3x8_1__6, decoder3x8_1__7, not_1_out, not_2_out, not_3_out,
       not_4_out, not_5_out, not_6_out, not_7_out, or_6_out, or_7_out, or_8_out, or_9_out, or_10_out,
       or_11_out, or_12_out, or_13_out, or_14_out, or_15_out, or_16_out, stepper_1_step_1, stepper_1_step_2,
       stepper_1_step_3, stepper_1_step_4, stepper_1_step_5, stepper_1_step_6, stepper_1_step_7;

  and and_1 (IAR_E, clke, or_6_out);
  and and_2 (RAM_E, clke, or_7_out);
  and and_3 (ACC_E, clke, or_8_out);
  and and_4 (IO_CLK_E, clke, and_47_out);
  or or_1 (Registry_0, and_5_out, and_9_out);
  or or_2 (Registry_1, and_6_out, and_10_out);
  or or_3 (Registry_2, and_7_out, and_11_out);
  or or_4 (Register_3, and_8_out, and_12_out);
  and and_5 (and_5_out, clke, or_9_out, decoder2x4_flipped_1__0);
  and and_6 (and_6_out, clke, or_9_out, decoder2x4_flipped_1__1);
  and and_7 (and_7_out, clke, or_9_out, decoder2x4_flipped_1__2);
  and and_8 (and_8_out, clke, or_9_out, decoder2x4_flipped_1__3);
  and and_9 (and_9_out, clke, or_10_out, decoder2x4_flipped_2__0);
  and and_10 (and_10_out, clke, or_10_out, decoder2x4_flipped_2__1);
  and and_11 (and_11_out, clke, or_10_out, decoder2x4_flipped_2__2);
  and and_12 (and_12_out, clke, or_10_out, decoder2x4_flipped_2__3);
  and and_13 (ALU_0, stepper_1_step_5, IR_IN[7], IR_IN[4]);
  and and_14 (ALU_1, stepper_1_step_5, IR_IN[7], IR_IN[5]);
  and and_15 (ALU_2, stepper_1_step_5, IR_IN[7], IR_IN[6]);
  or or_5 (Bus, and_17_out, and_38_out, and_37_out, and_34_out);
  or or_6 (or_6_out, and_17_out, and_34_out, and_36_out, and_37_out);
  or or_7 (or_7_out, stepper_1_step_2, and_50_out, and_45_out, and_44_out, and_42_out);
  or or_8 (or_8_out, stepper_1_step_3, and_46_out, and_49_out, and_48_out);
  or or_9 (or_9_out, and_31_out, and_43_out, and_35_out, and_39_out);
  or or_10 (or_10_out, and_33_out, and_32_out, C_2);
  and and_16 (and_16_out, clk, not_1_out);
  not not_1 (not_1_out, LOAD);
  not not_2 (not_2_out, LOAD);
  Decoder2x4_Flipped decoder2x4_flipped_1 (
    .a(IR_IN[0]), .b(IR_IN[1]), ._0(decoder2x4_flipped_1__0), ._1(decoder2x4_flipped_1__1),
    ._2(decoder2x4_flipped_1__2), ._3(decoder2x4_flipped_1__3));
  Decoder2x4_Flipped decoder2x4_flipped_2 (
    .a(IR_IN[2]), .b(IR_IN[3]), ._0(decoder2x4_flipped_2__0), ._1(decoder2x4_flipped_2__1),
    ._2(decoder2x4_flipped_2__2), ._3(decoder2x4_flipped_2__3));
  Stepper stepper_1 (
    .step_1(stepper_1_step_1), .step_2(stepper_1_step_2), .step_3(stepper_1_step_3),
    .step_4(stepper_1_step_4), .step_5(stepper_1_step_5), .step_6(stepper_1_step_6),
    .step_7(stepper_1_step_7), .reset(stepper_1_step_7), .clk(and_16_out));
  and and_17 (and_17_out, not_2_out, stepper_1_step_1);
  not not_3 (not_3_out, IR_IN[7]);
  Decoder3x8 decoder3x8_1 (
    .a(IR_IN[6]), .b(IR_IN[5]), .c(IR_IN[4]), ._0(decoder3x8_1__0), ._1(decoder3x8_1__1),
    ._2(decoder3x8_1__2), ._3(decoder3x8_1__3), ._4(decoder3x8_1__4), ._5(decoder3x8_1__5),
    ._6(decoder3x8_1__6), ._7(decoder3x8_1__7));
  and and_18 (and_18_out, not_3_out, decoder3x8_1__0);
  and and_19 (and_19_out, not_3_out, decoder3x8_1__1);
  and and_20 (and_20_out, not_3_out, decoder3x8_1__2);
  and and_21 (and_21_out, not_3_out, decoder3x8_1__3);
  and and_22 (and_22_out, not_3_out, decoder3x8_1__4);
  and and_23 (and_23_out, not_3_out, decoder3x8_1__5);
  and and_24 (and_24_out, not_3_out, decoder3x8_1__6);
  and and_25 (and_25_out, not_3_out, decoder3x8_1__7);
  not not_4 (not_4_out, IR_IN[5]);
  not not_5 (not_5_out, IR_IN[4]);
  and and_26 (and_26_out, C, IR_IN[3]);
  and and_27 (and_27_out, A, IR_IN[2]);
  and and_28 (and_28_out, E, IR_IN[1]);
  and and_29 (and_29_out, Z, IR_IN[0]);
  or or_11 (or_11_out, and_26_out, and_27_out, and_28_out, and_29_out);
  not not_6 (not_6_out, and_30_out);
  and and_30 (and_30_out, IR_IN[4], IR_IN[5], IR_IN[6]);
  and and_31 (and_31_out, stepper_1_step_4, IR_IN[7]);
  and and_32 (and_32_out, stepper_1_step_4, and_18_out);
  and and_33 (and_33_out, stepper_1_step_4, and_19_out);
  and and_34 (and_34_out, stepper_1_step_4, and_20_out);
  and and_35 (and_35_out, stepper_1_step_4, and_21_out);
  and and_36 (and_36_out, stepper_1_step_4, and_22_out);
  and and_37 (and_37_out, stepper_1_step_4, and_23_out);
  and and_38 (and_38_out, stepper_1_step_4, and_24_out);
  and and_39 (and_39_out, stepper_1_step_4, and_25_out, IR_IN[3]);
  and and_40 (END, IR_IN[7], IR_IN[6], not_4_out, not_5_out, stepper_1_step_4, IR_IN[3], IR_IN[2], IR_IN[1], IR_IN[0]);
  and and_41 (C_2, stepper_1_step_5, IR_IN[7]);
  and and_42 (and_42_out, stepper_1_step_5, and_18_out);
  and and_43 (and_43_out, stepper_1_step_5, and_19_out);
  and and_44 (and_44_out, stepper_1_step_5, and_20_out);
  and and_45 (and_45_out, stepper_1_step_5, and_22_out);
  and and_46 (and_46_out, stepper_1_step_5, and_23_out);
  not not_7 (not_7_out, IR_IN[3]);
  and and_47 (and_47_out, stepper_1_step_5, and_25_out, not_7_out);
  and and_48 (and_48_out, stepper_1_step_6, IR_IN[7], not_6_out);
  and and_49 (and_49_out, stepper_1_step_6, and_20_out);
  and and_50 (and_50_out, stepper_1_step_6, and_23_out, or_11_out);
  Decoder2x4 decoder2x4_1 (
    .a(IR_IN[0]), .b(IR_IN[1]), ._0(decoder2x4_1__0), ._1(decoder2x4_1__1), ._2(decoder2x4_1__2),
    ._3(decoder2x4_1__3));
  or or_12 (or_12_out, and_17_out, and_34_out, and_37_out, and_32_out, and_33_out, and_36_out);
  or or_13 (or_13_out, stepper_1_step_3, and_35_out, and_46_out, and_45_out, and_49_out, and_50_out);
  or or_14 (or_14_out, and_17_out, and_34_out, and_37_out, C_2);
  or or_15 (or_15_out, and_38_out, C_2);
  or or_16 (or_16_out, and_42_out, and_48_out, and_44_out, and_47_out);
  and and_51 (and_51_out, clks, stepper_1_step_2);
  and and_52 (and_52_out, clks, or_12_out);
  and and_53 (and_53_out, clks, or_13_out);
  and and_54 (and_54_out, clks, or_14_out);
  and and_55 (and_55_out, LOAD, clks);
  and and_56 (and_56_out, clks, and_43_out);
  and and_57 (and_57_out, clks, and_31_out);
  and and_58 (and_58_out, clks, or_15_out);
  and and_59 (IO_CLKS_S, clks, and_39_out);
  and and_60 (and_60_out, clks, or_16_out, decoder2x4_1__0);
  and and_61 (and_61_out, clks, or_16_out, decoder2x4_1__1);
  and and_62 (and_62_out, clks, or_16_out, decoder2x4_1__2);
  and and_63 (and_63_out, clks, or_16_out, decoder2x4_1__3);
  or or_17 (IR_S, RESET, and_51_out);
  or or_18 (MAR_S, MARS, and_52_out);
  or or_19 (IAR_S, RESET, and_53_out);
  or or_20 (ACC_S, RESET, and_54_out);
  or or_21 (RAM_S, and_55_out, and_56_out);
  or or_22 (TMP_S, RESET, and_57_out);
  or or_23 (FLAGS_S, RESET, and_58_out);
  or or_24 (R0_S, RESET, and_60_out);
  or or_25 (R1_S, RESET, and_61_out);
  or or_26 (R2_S, RESET, and_62_out);
  or or_27 (R3_S, RESET, and_63_out);

  assign DA = IR_IN[3];
  assign IO = IR_IN[2];

  // Notes on the sheet:
  //   REG A
  //   Register B
  //   Register A
endmodule

module Clock (
  input  clkin,
  output clk,
  output clks,
  output clke
);

  wire j_k_ff_1_qn, nand_1_out;

  J_K_Flip_Flop j_k_ff_1 (.J(1'b1), .clk(clkin), .K(1'b1), .Q(clk), .Qn(j_k_ff_1_qn));  // open: preset, en, reset
  nand nand_1 (nand_1_out, clkin, clk);
  nand nand_2 (clke, j_k_ff_1_qn, clkin);
  not not_1 (clks, nand_1_out);

  // Notes on the sheet:
  //   clkin: pull=down
  //   clk: pull=down
  //   clke: pull=down
  //   clks: pull=down
endmodule

module Decoder2x4 (
  input  a,
  input  b,
  output _0,
  output _1,
  output _2,
  output _3
);

  wire not_1_out, not_2_out;

  not not_1 (not_1_out, b);
  not not_2 (not_2_out, a);
  and and_1 (_0, not_2_out, not_1_out);
  and and_2 (_1, a, not_1_out);
  and and_3 (_2, b, not_2_out);
  and and_4 (_3, b, a);

  // Notes on the sheet:
  //   a: pull=down
  //   b: pull=down
endmodule

module Decoder2x4_Flipped (
  input  a,
  input  b,
  output _0,
  output _1,
  output _2,
  output _3
);

  wire not_1_out, not_2_out;

  not not_1 (not_1_out, b);
  not not_2 (not_2_out, a);
  and and_1 (_0, not_2_out, not_1_out);
  and and_2 (_1, a, not_1_out);
  and and_3 (_2, b, not_2_out);
  and and_4 (_3, b, a);

  // Notes on the sheet:
  //   b: pull=down
  //   a: pull=down
endmodule

module Decoder3x8 (
  input  a,
  input  b,
  input  c,
  output _0,
  output _1,
  output _2,
  output _3,
  output _4,
  output _5,
  output _6,
  output _7
);

  wire not_1_out, not_2_out, not_3_out;

  not not_1 (not_1_out, c);
  not not_2 (not_2_out, b);
  not not_3 (not_3_out, a);
  and and_1 (_0, not_3_out, not_2_out, not_1_out);
  and and_2 (_1, not_3_out, not_2_out, c);
  and and_3 (_2, not_3_out, b, not_1_out);
  and and_4 (_3, not_3_out, b, c);
  and and_5 (_4, a, not_2_out, not_1_out);
  and and_6 (_5, a, not_2_out, c);
  and and_7 (_6, a, b, not_1_out);
  and and_8 (_7, a, b, c);

  // Notes on the sheet:
  //   a: pull=down
  //   b: pull=down
  //   c: pull=down
endmodule

module CarryTemp (
  input  c,
  input  s,
  output o
);

  BasicMemory basicmemory_1 (.in_1(c), .in_2(s), .out_3(o));
endmodule

module _256_count_loader (
  input  clk,
  output [7:0] count,
  output carry
);

  wire counter_1_carry;

  Counter #(.ongoal("stay"), .trigger("falling")) counter_1 (
    .count(1'b1), .Q(count), .carry(counter_1_carry), .clk(clk));  // open: load, D, clr
  not not_1 (carry, counter_1_carry);
endmodule

module Delayer (
  input  [7:0] i,
  input  clk,
  output [7:0] o
);

  Counter #(.ongoal("stay"), .trigger("falling")) counter_1 (
    .load(1'b1), .D(i), .count(1'b0), .Q(o), .clk(clk));  // open: carry, clr
endmodule
